# Fritzing sketch lab1 (saved by Fritzing 0.9.3b)
breadboards: 1

parts:
  Part1 = Arduino Uno (Rev3) - ICSP
  S1 = SWITCH-MOMENTARY-2 [package=tactile-pth-12mm]
  R1 = Resistor [tolerance=±5% resistance=10k package="0805 [SMD]"]
  S2 = SWITCH-MOMENTARY-2 [package=tactile-pth-12mm]
  R2 = Resistor [tolerance=±5% resistance=10k package="0805 [SMD]"]
  R3 = TRIMPOT [package=trimpot-3mm]
  LED1 = Super Flux LED blue [color=Red]
  LED2 = Super Flux LED blue [color=Red]
  R4 = Resistor [tolerance=±5% resistance=330 package="0805 [SMD]"]
  R5 = Resistor [tolerance=±5% resistance=330 package="0805 [SMD]"]
  Touch_Sensor = TRIMPOT [package=trimpot-3mm]

nets:
  N1: Part1.A0, R3.WIPER
  N2: Part1.A1, Touch_Sensor.WIPER
  N3: Part1.5V, R1.Pin_0, R2.Pin_0, R3.CCW, Touch_Sensor.CCW
  N4: Part1.GND, S1.1, S2.1, R3.CW, R4.Pin_1, R5.Pin_1, Touch_Sensor.CW
  N5: Part1.D2, S1.2, R1.Pin_1
  N6: Part1.D3_PWM, S2.2, R2.Pin_1
  N7: Part1.D6_PWM, LED2.anode
  N8: Part1.D7, LED1.anode
  N9: LED1.cathode, R5.Pin_0
  N10: LED2.cathode, R4.Pin_0
